# Fritzing sketch ch_04_2N3904 (saved by Fritzing 0.8.7b)
breadboards: 1

parts:
  Part1 = Arduino Uno (Rev3) - ICSP
  R1 = Resistor [tolerance=±5% resistance=270 package=THT]
  M1 = DC Motor
  Q1 = NPN-Transistor [part_number=2N3904 package="TO92 [THT]"]
  VCC1 = 4 x AAA Battery Mount
  D1 = Diode [package=diode-1n4001]

nets:
  N1: Part1.ICSP_MOSI, Part1.D11_PWM/MOSI, R1.Pin_0
  N2: Part1.GND, Q1.E, VCC1.-
  N3: R1.Pin_1, Q1.B
  N4: M1.pin_1, VCC1.+, D1.A
  N5: M1.pin_2, Q1.C
