# Fritzing sketch ch_04_RGB_LED (saved by Fritzing 0.8.7b)
breadboards: 1

parts:
  R1 = Resistor [tolerance=±5% resistance=470 package=THT]
  LED1 = RGB LED (com. cathode, rbg) [package="5 mm [THT]"]
  R2 = Resistor [tolerance=±5% resistance=470 package=THT]
  R3 = Resistor [tolerance=±5% resistance=470 package=THT]
  VCC1 = Battery block 9V

nets:
  N1: R1.Pin_0, R2.Pin_0, R3.Pin_0, VCC1.+
  N2: R1.Pin_1, LED1.red_anode
  N3: LED1.common_cathode, VCC1.-
  N4: LED1.blue_anode, R2.Pin_1
  N5: LED1.green_anode, R3.Pin_1
